# Fritzing sketch Grill (saved by Fritzing 1.0.4)
breadboards: 1

parts:
  ESP = ESP32 DevKitc V4
  C1 = Capacitor Polarized [part_number="1000 µF" package=panasonic_e]
  J1 = screw terminal, 3 pins [part_number=0]
  WTV020-SD1 = WTV020-SD [part_number=WTV020-SD]
  SPKR1 = Loudspeaker
  R1 = Resistor [tolerance=±5% resistance=470 package="2512 [SMD]"]
  Neopixel-Ring = 16 NeoPixel Ring [part_number=1463]

nets:
  N1: ESP.CLK, WTV020-SD1.P04
  N2: ESP.D0, WTV020-SD1.P05
  N3: ESP.IO2, R1.Pin_0
  N4: ESP.GND#12, WTV020-SD1.GND
  3V3: ESP.3V3, WTV020-SD1.VDD
  N5: ESP.GND#32, C1.-, Neopixel-Ring.GND
  N6: C1.+, J1.pin3, Neopixel-Ring.VDD
  N7: J1.pin2, R1.Pin_1
  N8: WTV020-SD1.SPK+, SPKR1.pin1
  N9: WTV020-SD1.SPK-, SPKR1.pin2

custom parts:
  ESP32 DevKitc V4: ESP32-DevKitC board with ESP32-WROOM-32 module. ESP32-DevKitC V4 is a small-sized ESP32-based development board produced by Espressif. Most of the pins on the ESP module are broken out to the pin headers on the board. The pins D0, D1, D2, D3, CMD and CLK are used internally for communication between ESP32 and SPI flash memory. They are grouped on both sides near the USB connector. Avoid using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
  16 NeoPixel Ring: 16 ultra bright smart LED NeoPixels are arranged in a circle with 1.75" (44.5mm) outer diameter. The rings are 'chainable' - connect the output pin of one to the input pin of another. Use only one microcontroller pin to control as many as you can chain together! Each LED is addressable as the driver chip is inside the LED. Each one has ~18mA constant current drive so the color will be very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
